# Fritzing sketch n2k-pnm-v4-narrow (saved by Fritzing 0.9.6b)
circuit board: 8.5cm x 6cm

parts:
  U1 = Mini-360 DC-DC Buck converter [part_number="Reg 1" package=THT]
  Part1 = CAN transceiver mcp2552 Breakout
  Part2 = I2C level shifter bidirectional
  J3_12V_DC3 = Camdenboss CTB0158-2 [part_number=CTB0158-2 package=THT]
  C1 = Electrolytic Capacitor [capacitance=1µF voltage=35V package="100 mil [THT, electrolytic]"]
  R4 = Resistor [tolerance=±5% power=0.25 resistance=220 package=THT]
  D3 = Rectifier Diode [part_number=1N4001 package="300 mil [THT]"]
  Q2 = NPN-Transistor [package="TO92 [THT]"]
  R5 = Resistor [tolerance=±5% power=0.25 resistance=220 package=THT]
  J4_AIS_IN1 = Camdenboss CTB0158-2 [part_number=CTB0158-2 package=THT]
  R6 = Resistor [tolerance=±5% power=0.25 resistance=220 package=THT]
  D4 = Rectifier Diode [part_number=1N4001 breakdown_voltage=3.6V package="300 mil [THT]"]
  LED1 = LED - 3mm [color="Green (570nm)" current=0.030 package="3 mm [THT]"]
  R7 = Resistor [tolerance=±5% power=0.25 resistance=220 package=THT]
  R8 = Resistor [tolerance=±5% power=0.25 resistance=220 package=THT]
  J1 = male pin header, 8 pins [form="♂ (male)" part_number="3v3 IO"]
  J3 = male pin header, 3 pins [form="♂ (male)"]
  U2 = ESP32S-HiLetgo [part_number=ESP32S-HiLetgo]
  J3_12V_DC2 = Camdenboss CTB0158-2 [part_number=CTB0158-2 package=THT]
  J4 = male pin header, 4 pins [form="♂ (male)"]
  J2 = male pin header, 4 pins [form="♂ (male)"]
  J10 = female pin header, 8 pins [form="♀ (female)"]
  J6 = female pin header, 8 pins [form="♀ (female)"]
  J7 = female pin header, 8 pins [form="♀ (female)"]
  J8 = female pin header, 8 pins [form="♀ (female)"]
  J9 = female pin header, 8 pins [form="♀ (female)"]
  J11 = female pin header, 8 pins [form="♀ (female)"]

nets (from the pcb view):
  GND: U1.IN-, U1.OUT-, Part1.GND, Part2.GND, C1.-, D3.anode, Q2.E, J4_AIS_IN1.pin1, LED1.cathode, R8.Pin_1, J1.pin8, J3.pin1, U2.GND, J3_12V_DC2.pin1, J4.pin4, J2.pin4, J11.pin1, J11.pin2, J11.pin3, J11.pin4, J11.pin5, J11.pin6, J11.pin7, J11.pin8
  N1: U1.IN+, D4.cathode, R7.Pin_1
  VCC: U1.OUT+, Part1.VCC, Part2.HV, R6.Pin_0, U2.VIN, J4.pin1
  N2: Part1.CANL, J3_12V_DC3.pin1
  N3: Part1.CANH, J3_12V_DC3.pin2
  N4: Part1.RXD, Part2.HV4
  N5: Part1.TXD, Part2.HV3
  N6: Part2.LV4, U2.GPIO4
  N7: Part2.LV3, U2.GPIO5
  N8: Part2.LV, R5.Pin_0, J1.pin1, U2.3.3, J2.pin1, J10.pin1, J10.pin2, J10.pin3, J10.pin4, J10.pin5, J10.pin6, J10.pin7, J10.pin8
  N9: Part2.LV2, U2.GPIO18
  N10: Part2.LV1, U2.GPIO19
  N11: Part2.HV1, J4.pin3
  N12: Part2.HV2, J4.pin2
  N13: C1.+, U2.EN
  N14: R4.Pin_0, D3.cathode, Q2.B
  N15: R4.Pin_1, J4_AIS_IN1.pin2
  N16: Q2.C, R5.Pin_1, U2.GPIO16
  N17: R6.Pin_1, LED1.anode
  N18: D4.anode, J3_12V_DC2.pin2
  N19: R7.Pin_0, R8.Pin_0, U2.GPIO34
  N20: J1.pin2, U2.GPIO32
  N21: J1.pin3, U2.GPIO33
  N22: J1.pin4, U2.GPIO25
  N23: J1.pin5, U2.GPIO26
  N24: J1.pin6, U2.GPIO27
  N25: J1.pin7, U2.GPIO14
  N26: J3.pin2, U2.GPIO1
  N27: J3.pin3, U2.GPIO3
  N28: U2.GPIO21, J2.pin3
  N29: U2.GPIO22, J2.pin2
  N30: J6.pin1, J6.pin2, J6.pin3, J6.pin4, J6.pin5, J6.pin6, J6.pin7, J6.pin8
  N31: J7.pin1, J7.pin2, J7.pin3, J7.pin4, J7.pin5, J7.pin6, J7.pin7, J7.pin8
  N32: J8.pin1, J8.pin2, J8.pin3, J8.pin4, J8.pin5, J8.pin6, J8.pin7, J8.pin8
  N33: J9.pin1, J9.pin2, J9.pin3, J9.pin4, J9.pin5, J9.pin6, J9.pin7, J9.pin8

notes:
  +
  -
  12V
  H CAN L
  + AIS -
  Naiad N2k GW 1.0
  GND
  SDA
  SCL
  3v3
  RXD
  TXD
  32
  33
  25
  26
  27
  14
  19
  18
  5V I/O
  3v3 I/O
  +5V

custom parts:
  Mini-360 DC-DC Buck converter: Mini-360 DC-DC Buck converter. Tiny buck step down voltage converter, input voltage 4.75 to 23V output 1 to 17V adjustable. Available from ebay and the like.
  CAN transceiver mcp2552 Breakout: Description: This is a breakout board for the MCP2552 CAN bus transceiver
  ESP32S-HiLetgo: HiLetgo ESP-WROOM-32 ESP32 ESP-32S Development Board 2.4GHz Dual-Mode WiFi + Bluetooth Dual Cores Microcontroller The ESP32 integrated with Antenna switches, RF Balun, power amplifiers, low-noise amplifiers, filters, and management modules, and the entire solution occupies the least area of PCB. 2.4 GHz Wi-Fi plus Bluetooth dual-mode chip, with TSMC Ultra-low power consumption 40nm technology,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
